// Logisim project Boba Vending Machine.circ as structural Verilog: 5 circuits, main circuit main
module Money_Input (
  input  _1,
  input  _5,
  input  _10,
  input  _25,
  input  _50,
  input  _1_2,
  input  _5_2,
  input  _10_2,
  input  _20,
  output [11:0] out_10
);

  wire n12_bit_super_adder_1_out_11;
  wire [11:0] adder_1_out, n12_bit_super_adder_1_total;

  _12_bit_super_adder u_12_bit_super_adder_1 (
    .in_1({{11{1'b0}}, _1}), .in_2({{9{1'b0}}, _5, 1'b0, _5}), .in_3({{8{1'b0}}, _10, 1'b0, _10, 1'b0}),
    .in_4({{7{1'b0}}, {2{_25}}, 2'b00, _25}), .in_5({{6{1'b0}}, {2{_50}}, 2'b00, _50, 1'b0}),
    .in_6({{5{1'b0}}, {2{_1_2}}, 2'b00, _1_2, 2'b00}), .in_7({3'b000, {5{_5_2}}, 1'b0, _5_2, 2'b00}),
    .in_8({2'b00, {5{_10_2}}, 1'b0, _10_2, 3'b000}), .in_9({1'b0, {5{_20}}, 1'b0, _20, 4'b0000}),
    .Total(n12_bit_super_adder_1_total), .out_11(n12_bit_super_adder_1_out_11));
  Adder #(.width(12)) adder_1 (.a(n12_bit_super_adder_1_total), .b(out_10), .out(adder_1_out));  // open: cin, cout
  Register #(.width(12)) register_1 (.D(adder_1_out), .Q(out_10), .clk(n12_bit_super_adder_1_out_11));  // open: en, clr
endmodule

module main (
  output [2:0] out_1
);

  wire button_1_out, button_2_out, button_3_out, button_4_out, button_5_out, button_6_out, button_7_out,
       button_8_out, button_9_out, button_10_out, button_11_out, button_12_out, Clr_out;
  wire [3:0] main_1_p2, main_1_p3, main_1_p4, main_1_p5, main_2_p2, main_2_p3, main_2_p4, main_2_p5;
  wire [11:0] flavor_input_1_price, money_input_1_out_10;

  LED Not_Enough_Money ();  // open: in
  LED led_1 ();  // open: in
  LED led_2 ();  // open: in
  LED led_3 ();  // open: in
  Button button_1 (.out(button_1_out));
  Button button_2 (.out(button_2_out));
  Button button_3 (.out(button_3_out));
  Button button_4 (.out(button_4_out));
  Button button_5 (.out(button_5_out));
  Button button_6 (.out(button_6_out));
  Button button_7 (.out(button_7_out));
  Button button_8 (.out(button_8_out));
  Button button_9 (.out(button_9_out));
  Button button_10 (.out(button_10_out));
  Button button_11 (.out(button_11_out));
  Button button_12 (.out(button_12_out));
  Button Buy ();  // open: out
  Money_Input money_input_1 (
    ._1(button_1_out), ._5(button_2_out), ._10(button_3_out), ._25(button_4_out), ._50(button_5_out),
    ._1_2(button_6_out), ._5_2(button_7_out), ._10_2(button_8_out), ._20(button_9_out),
    .out_10(money_input_1_out_10));
  Flavor_Input flavor_input_1 (
    .in_1(button_10_out), .Price(flavor_input_1_price), .Flavor(out_1), .in_2(button_11_out),
    .in_3(button_12_out), .in_4(Clr_out));
  Button Clr (.out(Clr_out));
  Hex_Digit_Display hex_digit_display_1 (.value(main_1_p2));  // open: dp
  Hex_Digit_Display hex_digit_display_2 (.value(main_1_p3));  // open: dp
  Hex_Digit_Display hex_digit_display_3 (.value(main_1_p4));  // open: dp
  Hex_Digit_Display hex_digit_display_4 (.value(main_1_p5));  // open: dp
  // _12_Bit_BCD_Converter__Final___1__main main_1: pin names not known; wires that end beside it: money_input_1_out_10, main_1_p2, main_1_p3, main_1_p4, main_1_p5
  // _12_Bit_BCD_Converter__Final___1__main main_2: pin names not known; wires that end beside it: flavor_input_1_price, main_2_p2, main_2_p3, main_2_p4, main_2_p5
  Hex_Digit_Display hex_digit_display_5 (.value(main_2_p2));  // open: dp
  Hex_Digit_Display hex_digit_display_6 (.value(main_2_p3));  // open: dp
  Hex_Digit_Display hex_digit_display_7 (.value(main_2_p4));  // open: dp
  Hex_Digit_Display hex_digit_display_8 (.value(main_2_p5));  // open: dp
  LED led_4 (.in(out_1[0]));
  LED led_5 (.in(out_1[1]));
  LED led_6 (.in(out_1[2]));

  // Notes on the sheet:
  //   Money Input
  //   Flavor
  //   Total:
  //   Change:
endmodule

module Flavor_Input (
  input  in_1,
  input  in_2,
  input  in_3,
  input  in_4,
  output [11:0] Price,
  output [2:0] Flavor
);

  wire comparator_1_eq, not_1_out;

  Comparator #(.width(3)) comparator_1 (.a({in_3, in_2, in_1}), .b(3'b000), .eq(comparator_1_eq));  // open: gt, lt
  not not_1 (not_1_out, comparator_1_eq);
  Register #(.width(3)) register_1 (.D({in_3, in_2, in_1}), .en(not_1_out), .Q(Flavor), .clk(not_1_out), .clr(in_4));
  Flavor_State flavor_state_1 (
    .a(Flavor[0]), .b(Flavor[1]), .c(Flavor[2]), .x(Price[11]), .y(Price[10]), .z(Price[9]), .u(Price[8]),
    .v(Price[7]), .w(Price[6]), .s(Price[5]), .t(Price[4]), .x2(Price[3]), .x3(Price[2]), .x4(Price[1]),
    .x5(Price[0]));
endmodule

module Flavor_State (
  input  a,
  input  b,
  input  c,
  output x,
  output y,
  output z,
  output u,
  output v,
  output w,
  output s,
  output t,
  output x2,
  output x3,
  output x4,
  output x5
);

  wire and_2_out, and_3_out, and_5_out, and_6_out, and_7_out, and_10_out, and_11_out, and_12_out, and_13_out,
       not_1_out, not_2_out, not_3_out, not_4_out, not_5_out, not_6_out, not_7_out, not_8_out, not_9_out,
       not_10_out, not_11_out, not_12_out, not_13_out, not_14_out, not_15_out, not_16_out, not_17_out,
       not_18_out, not_19_out, not_20_out, not_21_out, not_22_out, not_23_out, not_24_out, not_25_out,
       not_26_out, not_27_out, not_28_out;

  not not_1 (not_1_out, a);
  not not_2 (not_2_out, b);
  not not_3 (not_3_out, a);
  not not_4 (not_4_out, c);
  not not_5 (not_5_out, b);
  not not_6 (not_6_out, c);
  not not_7 (not_7_out, a);
  not not_8 (not_8_out, c);
  not not_9 (not_9_out, a);
  not not_10 (not_10_out, b);
  not not_11 (not_11_out, a);
  not not_12 (not_12_out, c);
  not not_13 (not_13_out, b);
  not not_14 (not_14_out, c);
  not not_15 (not_15_out, b);
  not not_16 (not_16_out, c);
  not not_17 (not_17_out, a);
  not not_18 (not_18_out, b);
  not not_19 (not_19_out, a);
  not not_20 (not_20_out, b);
  not not_21 (not_21_out, b);
  not not_22 (not_22_out, c);
  not not_23 (not_23_out, a);
  not not_24 (not_24_out, c);
  not not_25 (not_25_out, b);
  not not_26 (not_26_out, c);
  not not_27 (not_27_out, b);
  not not_28 (not_28_out, c);
  and and_1 (y, not_1_out, not_2_out, c);
  and and_2 (and_2_out, not_3_out, b, not_4_out);
  and and_3 (and_3_out, a, not_5_out, not_6_out);
  and and_4 (u, not_7_out, b, not_8_out);
  and and_5 (and_5_out, not_9_out, not_10_out, c);
  and and_6 (and_6_out, not_11_out, b, not_12_out);
  and and_7 (and_7_out, a, not_13_out, not_14_out);
  and and_8 (w, a, not_15_out, not_16_out);
  and and_9 (s, not_17_out, not_18_out, c);
  and and_10 (and_10_out, not_19_out, not_20_out, c);
  and and_11 (and_11_out, a, not_21_out, not_22_out);
  and and_12 (and_12_out, not_23_out, b, not_24_out);
  and and_13 (and_13_out, a, not_25_out, not_26_out);
  and and_14 (x5, a, not_27_out, not_28_out);
  or or_1 (z, and_2_out, and_3_out);
  or or_2 (v, and_5_out, and_6_out, and_7_out);
  or or_3 (t, and_10_out, and_11_out);
  or or_4 (x3, and_12_out, and_13_out);

  assign x = 1'b0;
  assign x2 = 1'b0;
  assign x4 = 1'b0;
endmodule

// Super adder
module _12_bit_super_adder (
  input  [11:0] in_1,
  input  [11:0] in_2,
  input  [11:0] in_3,
  input  [11:0] in_4,
  input  [11:0] in_5,
  input  [11:0] in_6,
  input  [11:0] in_7,
  input  [11:0] in_8,
  input  [11:0] in_9,
  output [11:0] Total,
  output out_11
);

  wire [11:0] adder_1_out, adder_2_out, adder_3_out, adder_4_out, adder_5_out, adder_6_out, adder_7_out;

  Adder #(.width(12)) adder_1 (.a(in_1), .b(in_2), .out(adder_1_out));  // open: cin, cout
  Adder #(.width(12)) adder_2 (.a(in_3), .b(in_4), .out(adder_2_out));  // open: cin, cout
  Adder #(.width(12)) adder_3 (.a(in_5), .b(in_6), .out(adder_3_out));  // open: cin, cout
  Adder #(.width(12)) adder_4 (.a(in_7), .b(in_8), .out(adder_4_out));  // open: cin, cout
  Adder #(.width(12)) adder_5 (.a(adder_1_out), .b(adder_2_out), .out(adder_5_out));  // open: cin, cout
  Adder #(.width(12)) adder_6 (.a(adder_3_out), .b(adder_4_out), .out(adder_6_out));  // open: cin, cout
  Adder #(.width(12)) adder_7 (.a(adder_5_out), .b(adder_6_out), .out(adder_7_out));  // open: cin, cout
  Adder #(.width(12)) adder_8 (.a(adder_7_out), .b(in_9), .out(Total));  // open: cin, cout
  Comparator #(.width(12)) comparator_1 (.a(Total), .b({12{1'b0}}), .gt(out_11));  // open: eq, lt
endmodule
